// Logisim project FSM.circ as structural Verilog: 4 circuits, main circuit FSM
module FSM (
  input  FSM_Input,
  output FSM_Output
);

  wire clock_1_out;
  wire [1:0] FSM_next_state_f51ac6e5, register_1_q;

  FSMLogic FSM (
    .Input(FSM_Input), .Current_State(register_1_q), .Output(FSM_Output),
    .Next_State_f51ac6e5(FSM_next_state_f51ac6e5));
  Register #(.width(2)) register_1 (.D(FSM_next_state_f51ac6e5), .Q(register_1_q), .clk(clock_1_out));  // open: en, clr
  Clock clock_1 (.out(clock_1_out));
endmodule

module FSMLogic (
  input  Input,
  input  [1:0] Current_State,
  output Output,
  output [1:0] Next_State_f51ac6e5
);

  wire and_1_out, and_2_out, not_1_out, not_2_out, not_3_out;

  not not_1 (not_1_out, Input);
  not not_2 (not_2_out, Current_State[0]);
  not not_3 (not_3_out, Current_State[1]);
  and and_1 (and_1_out, Input, not_3_out);
  and and_2 (and_2_out, not_1_out, not_2_out);
  StateBitZero statebitzero_1 (
    .Input(Input), .State_Bit_0(Current_State[0]), .State_Bit_1(Current_State[1]),
    .New_State_0_13864c51(Next_State_f51ac6e5[0]));
  StateBitOne statebitone_1 (
    .Input(Input), .State_Bit_0(Current_State[0]), .State_Bit_1(Current_State[1]),
    .New_State_1_8ee173aa(Next_State_f51ac6e5[1]));
  or or_1 (Output, and_1_out, and_2_out);
endmodule

module StateBitOne (
  input  Input,
  input  State_Bit_0,
  input  State_Bit_1,
  output New_State_1_8ee173aa
);

  // NOT_Gate not_1 has open pins: in=Input, out=open
  // NOT_Gate not_2 has open pins: in=State_Bit_0, out=open
  // NOT_Gate not_3 has open pins: in=State_Bit_1, out=open
  or or_1 (New_State_1_8ee173aa, Input, State_Bit_0);

  // Notes on the sheet:
  //   PUT CIRCUITRY HERE
endmodule

module StateBitZero (
  input  Input,
  input  State_Bit_0,
  input  State_Bit_1,
  output New_State_0_13864c51
);

  wire and_1_out, and_2_out, and_3_out, and_4_out, not_2_out, not_3_out;

  // NOT_Gate not_1 has open pins: in=Input, out=open
  not not_2 (not_2_out, State_Bit_0);
  not not_3 (not_3_out, State_Bit_1);
  and and_1 (and_1_out, Input, State_Bit_0);
  and and_2 (and_2_out, not_2_out, not_3_out);
  and and_3 (and_3_out, and_1_out, not_3_out);
  and and_4 (and_4_out, Input, and_2_out);
  or or_1 (New_State_0_13864c51, and_3_out, and_4_out);

  // Notes on the sheet:
  //   PUT CIRCUITRY HERE
endmodule
