// Logisim project lab5.circ as structural Verilog: 10 circuits, main circuit main
module main (
  input  in_1,
  input  in_2,
  output out_3,
  output [7:0] out_4,
  output [7:0] out_5
);

  AddMachine addmachine_1 (.out_1(out_4), .out_2(out_5));
  and and_1 (out_3, in_1, in_2);
endmodule

module NAND (
  input  in_1,
  input  in_2,
  input  in_3,
  input  in_4,
  output out_5,
  output out_6
);

  wire and_1_out;

  and and_1 (and_1_out, in_1, in_2);
  nand nand_1 (out_6, in_3, in_4);
  not not_1 (out_5, and_1_out);
endmodule

module NOR (
  input  in_1,
  input  in_2,
  input  in_3,
  input  in_4,
  output out_5,
  output out_6
);

  wire or_1_out;

  or or_1 (or_1_out, in_1, in_2);
  nor nor_1 (out_6, in_3, in_4);
  not not_1 (out_5, or_1_out);
endmodule

module XOR (
  input  in_1,
  input  in_2,
  input  in_3,
  input  in_4,
  output out_5,
  output out_6
);

  wire nor_1_out, nor_2_out, nor_3_out, nor_4_out;

  nor nor_1 (nor_1_out, in_1, in_1);
  nor nor_2 (nor_2_out, in_2, in_2);
  nor nor_3 (nor_3_out, nor_1_out, nor_2_out);
  nor nor_4 (nor_4_out, in_2, in_1);
  xor xor_1 (out_6, in_3, in_4);
  nor nor_5 (out_5, nor_3_out, nor_4_out);
endmodule

module _2_to_1_MUX (
  input  in_1,
  input  S,
  input  in_3,
  output out_4
);

  wire and_1_out, and_2_out, not_1_out;

  not not_1 (not_1_out, S);
  and and_1 (and_1_out, in_1, not_1_out);
  and and_2 (and_2_out, S, in_3);
  or or_1 (out_4, and_1_out, and_2_out);
endmodule

module _4_to_1_MUX (
  input  S1,
  input  S2,
  input  in_3,
  input  in_4,
  input  in_5,
  input  in_6,
  output out_7
);

  wire n2_to_1_mux_1_out_4, n2_to_1_mux_2_out_4;

  _2_to_1_MUX u_2_to_1_mux_1 (.in_1(in_3), .S(S1), .in_3(in_4), .out_4(n2_to_1_mux_1_out_4));
  _2_to_1_MUX u_2_to_1_mux_2 (.in_1(in_5), .S(S1), .in_3(in_6), .out_4(n2_to_1_mux_2_out_4));
  _2_to_1_MUX u_2_to_1_mux_3 (.in_1(n2_to_1_mux_1_out_4), .S(S2), .in_3(n2_to_1_mux_2_out_4), .out_4(out_7));
endmodule

module AddMachine (
  output [7:0] out_1,
  output [7:0] out_2
);

  wire clock_1_out;

  Clock clock_1 (.out(clock_1_out));
  Register register_1 (.D(out_1), .Q(out_2), .clk(clock_1_out));  // open: en, clr
  Adder adder_1 (.a(8'h1), .b(out_2), .out(out_1));  // open: cin, cout
endmodule

module Ex4 (
  input  [7:0] In,
  output Out1,
  output [7:0] Out1_2
);

  not not_1 (Out1_2[7], In[7]);
  and and_1 (Out1, In[0], In[7]);

  assign Out1_2[6:0] = In[6:0];
endmodule

module rotr (
  input  [15:0] in_1,
  input  [3:0] in_2,
  output [15:0] out_3
);

  wire [15:0] mux1, mux2, mux3, shift1_2_out_2, shift1_3_out_2, shift1_7_out_2, shift1_8_out_2,
       shift1_9_out_2, shift1_10_out_2, shift1_11_out_2, shift1_12_out_2, shift1_13_out_2, shift1_14_out_2,
       shift1_15_out_2, undriven, undriven_2, undriven_3, undriven_4;

  shift1 shift1_1 (.in_1(shift1_2_out_2), .out_2(mux3));
  shift1 shift1_2 (.in_1(shift1_3_out_2), .out_2(shift1_2_out_2));
  shift1 shift1_3 (.in_1(shift1_8_out_2), .out_2(shift1_3_out_2));
  shift1 shift1_4 (.in_1(undriven), .out_2(in_1));
  shift1 shift1_5 (.in_1(shift1_9_out_2), .out_2(mux1));
  shift1 shift1_6 (.in_1(shift1_10_out_2), .out_2(mux2));
  shift1 shift1_7 (.in_1(shift1_13_out_2), .out_2(shift1_7_out_2));
  shift1 shift1_8 (.in_1(shift1_7_out_2), .out_2(shift1_8_out_2));
  shift1 shift1_9 (.in_1(undriven_2), .out_2(shift1_9_out_2));
  shift1 shift1_10 (.in_1(shift1_11_out_2), .out_2(shift1_10_out_2));
  shift1 shift1_11 (.in_1(shift1_14_out_2), .out_2(shift1_11_out_2));
  shift1 shift1_12 (.in_1(shift1_15_out_2), .out_2(shift1_12_out_2));
  shift1 shift1_13 (.in_1(shift1_12_out_2), .out_2(shift1_13_out_2));
  Multiplexer #(.width(16), .enable("false")) multiplexer_1 (.in0(in_1), .in1(undriven), .out(mux1), .sel(in_2[0]));
  Multiplexer #(.width(16), .enable("false")) multiplexer_2 (.in0(mux1), .in1(undriven_2), .out(mux2), .sel(in_2[1]));
  shift1 shift1_14 (.in_1(undriven_3), .out_2(shift1_14_out_2));
  shift1 shift1_15 (.in_1(undriven_4), .out_2(shift1_15_out_2));
  Multiplexer #(.width(16), .enable("false")) multiplexer_3 (.in0(mux2), .in1(undriven_3), .out(mux3), .sel(in_2[2]));
  Multiplexer #(.width(16), .enable("false")) multiplexer_4 (.in0(mux3), .in1(undriven_4), .out(out_3), .sel(in_2[3]));

  // Other names for the same wires on the sheet: select1 = in_2[0]; select2 = in_2[1]; select3 = in_2[2];
  //   select4 = in_2[3]; Input[15:0] = in_1; Output[15:0] = out_3
endmodule

module shift1 (
  input  [15:0] in_1,
  output [15:0] out_2
);


  assign out_2 = {in_1[0], in_1[15:1]};
endmodule
