// Logisim project cpuyolo.circ as structural Verilog: 5 circuits, main circuit main
module main (
  input  [31:0] INSTRUCTION,
  input  CLOCK,
  output [31:0] FETCH_ADDRESS,
  output [31:0] ra_Value,
  output [31:0] sp_Value,
  output [31:0] t0_Value,
  output [31:0] t1_Value,
  output [31:0] t2_Value,
  output [31:0] s0_Value,
  output [31:0] s1_Value,
  output [31:0] a0_Value
);

  wire ASel, BrEq, BrLT, BRUn, BSel, MemRW, PCSel, RegWEn;
  wire [1:0] WBSel;
  wire [2:0] funct3, ImmSel;
  wire [3:0] ALUSel;
  wire [4:0] rd, rs1, rs2;
  wire [6:0] funct7, opcode;
  wire [31:0] ALUResult, immediate, MEM_read_data, multiplexer_1_out, multiplexer_2_out, multiplexer_3_out,
       PC, PC_4, rs1_data, rs2_data, writeData;

  Multiplexer #(.width(32), .enable("false")) multiplexer_1 (
    .in0(PC_4), .in1(ALUResult), .out(multiplexer_1_out), .sel(PCSel));
  Shifter #(.width(32), .shift("lr")) shifter_1 (.in(PC), .\dist (5'b00010), .out(FETCH_ADDRESS));
  Register #(.width(32)) u_PC (.D(multiplexer_1_out), .Q(PC), .clk(CLOCK));  // open: en, clr
  SplitInstruction splitinstruction_1 (
    .Instruction(INSTRUCTION), .opcode(opcode), .rd(rd), .funct3(funct3), .rs1(rs1), .rs2(rs2),
    .funct7(funct7));
  BranchComp branchcomp_1 (.rs1(rs1_data), .rs2(rs2_data), .BrUn(BRUn), .BrEq(BrEq), .BrLT(BrLT));
  Control control_1 (
    .opcode(opcode), .funct3(funct3), .funct7(funct7), .BrEq(BrEq), .BrLT(BrLT), .RegWEn(RegWEn),
    .MemRW(MemRW), .PCSel(PCSel), .BrUn(BRUn), .BSel(BSel), .ASel(ASel), .ImmSel(ImmSel), .WBSel(WBSel),
    .ALUSel(ALUSel));
  ImmGen immgen_1 (.instruction(INSTRUCTION), .ImmSel(ImmSel), .immediate(immediate));
  Adder #(.width(32)) adder_1 (.a(PC), .b(32'h4), .out(PC_4));  // open: cin, cout
  regfile_main main_1 (
    .Read_Register_1__rs1(rs1), .Read_Register_2__rs2(rs2), .Write_Register__rd(rd), .Write_Data(writeData),
    .Write_Enable(RegWEn), .Clock(CLOCK), .Read_Data_1(rs1_data), .Read_Data_2(rs2_data),
    .ra_Value(ra_Value), .sp_Value(sp_Value), .t0_Value(t0_Value), .t1_Value(t1_Value), .t2_Value(t2_Value),
    .s0_Value(s0_Value), .s1_Value(s1_Value), .a0_Value(a0_Value));
  Multiplexer #(.width(32), .enable("false")) multiplexer_2 (
    .in0(rs1_data), .in1(PC), .out(multiplexer_2_out), .sel(ASel));
  Multiplexer #(.width(32), .enable("false")) multiplexer_3 (
    .in0(rs2_data), .in1(immediate), .out(multiplexer_3_out), .sel(BSel));
  alu_main main_2 (.Switch(ALUSel), .X(multiplexer_2_out), .Result(ALUResult), .Y(multiplexer_3_out));  // open: Equal
  mem_main MEM (.Address(ALUResult), .Write_Data(rs2_data), .Write_En(MemRW), .Clock(CLOCK), .Read_Data(MEM_read_data));
  Multiplexer #(.select(2), .width(32), .enable("false")) multiplexer_4 (
    .in0(MEM_read_data), .in1(ALUResult), .in2(PC_4), .out(writeData), .sel(WBSel));  // open: in3
  // AND_Gate and_1 is placed but not wired

  // Other names for the same wires on the sheet: clk = CLOCK; fetch_addr[31:0] = FETCH_ADDRESS; x1[31:0] = ra_Value;
  //   x2[31:0] = sp_Value; x5[31:0] = t0_Value; x6[31:0] = t1_Value; x7[31:0] = t2_Value; x8[31:0] = s0_Value;
  //   x9[31:0] = s1_Value; x10[31:0] = a0_Value

  // Notes on the sheet:
  //   Output
  //   These are outputs/inputs from run.circ
  //   Inputs
endmodule

module SplitInstruction (
  input  [31:0] Instruction,
  output [6:0] opcode,
  output [4:0] rd,
  output [2:0] funct3,
  output [4:0] rs1,
  output [4:0] rs2,
  output [6:0] funct7
);


  assign funct3 = Instruction[14:12];
  assign funct7 = Instruction[31:25];
  assign opcode = Instruction[6:0];
  assign rd = Instruction[11:7];
  assign rs1 = Instruction[19:15];
  assign rs2 = Instruction[24:20];
endmodule

module Control (
  input  [6:0] opcode,
  input  [2:0] funct3,
  input  [6:0] funct7,
  input  BrEq,
  input  BrLT,
  output RegWEn,
  output MemRW,
  output PCSel,
  output BrUn,
  output BSel,
  output ASel,
  output [2:0] ImmSel,
  output [1:0] WBSel,
  output [3:0] ALUSel
);

  wire and_1_out, and_2_out, and_3_out, and_4_out, and_5_out, and_6_out, and_7_out, and_8_out, and_9_out,
       and_10_out, and_11_out, and_12_out, and_13_out, and_14_out, and_15_out, and_16_out, and_17_out,
       and_18_out, and_19_out, and_20_out, and_21_out, and_22_out, and_23_out, and_24_out, and_25_out,
       and_27_out, and_28_out, and_29_out, and_30_out, and_31_out, and_32_out, and_33_out, and_34_out,
       and_35_out, and_36_out, and_37_out, and_38_out, and_39_out, f3_0, f3_1, f3_2, f3_4, f3_5, f3_6, f3_7,
       f7_0, f7_1, f7_2, IType1, IType2, IType3, or_1_out, or_2_out, or_3_out, or_4_out, or_5_out, or_6_out,
       or_7_out, or_8_out, or_9_out, or_11_out, or_12_out, or_14_out, or_15_out, or_16_out, or_17_out,
       or_18_out, or_19_out, or_20_out, or_21_out, RType, SBType, UJType, UType;
  wire [1:0] controlled_buffer_13_out, multiplexer_3_out, multiplexer_6_out;
  wire [2:0] multiplexer_1_out, multiplexer_2_out, multiplexer_5_out;
  wire [3:0] controlled_buffer_1_out, multiplexer_4_out, multiplexer_7_out, multiplexer_10_out,
       multiplexer_11_out, multiplexer_12_out, multiplexer_13_out, multiplexer_14_out, multiplexer_15_out,
       multiplexer_16_out, multiplexer_17_out, multiplexer_18_out;

  or or_1 (or_1_out, f3_4, f3_6);
  Multiplexer #(.width(3), .enable("false")) multiplexer_1 (
    .in0(3'b100), .in1(3'b011), .out(multiplexer_1_out), .sel(UType));
  Multiplexer #(.width(3), .enable("false")) multiplexer_2 (
    .in0(multiplexer_1_out), .in1(3'b010), .out(multiplexer_2_out), .sel(SBType));
  Multiplexer #(.width(2), .enable("false")) multiplexer_3 (
    .in0(2'b00), .in1(2'b10), .out(multiplexer_3_out), .sel(or_2_out));
  or or_2 (or_2_out, UJType, IType3);
  Multiplexer #(.width(4), .enable("false")) multiplexer_4 (
    .in0(4'b0000), .in1(4'b1100), .out(multiplexer_4_out), .sel(and_1_out));
  and and_1 (and_1_out, RType, f3_0, f7_2);
  and and_2 (and_2_out, RType, f3_0, f7_0);
  and and_3 (and_3_out, f3_0, IType2);
  and and_4 (and_4_out, RType, f3_6, f7_0);
  and and_5 (and_5_out, IType2, f3_6);
  and and_6 (and_6_out, RType, f3_4, f7_0);
  and and_7 (and_7_out, IType2, f3_4);
  and and_8 (and_8_out, RType, f3_5, f7_0);
  and and_9 (and_9_out, IType2, f3_5, f7_0);
  and and_10 (and_10_out, RType, f3_1, f7_0);
  and and_11 (and_11_out, IType2, f3_1, f7_0);
  and and_12 (and_12_out, RType, f3_2, f7_0);
  and and_13 (and_13_out, IType2, f3_2);
  and and_14 (and_14_out, SBType, f3_0, BrEq);
  and and_15 (and_15_out, SBType, or_1_out, BrLT);
  Multiplexer #(.width(3), .enable("false")) multiplexer_5 (
    .in0(multiplexer_2_out), .in1(3'b001), .out(multiplexer_5_out), .sel(MemRW));
  Multiplexer #(.width(2), .enable("false")) multiplexer_6 (
    .in0(multiplexer_3_out), .in1(2'b01), .out(multiplexer_6_out), .sel(or_3_out));
  or or_3 (or_3_out, RType, IType2, UType);
  Multiplexer #(.width(4), .enable("false")) multiplexer_7 (
    .in0(multiplexer_4_out), .in1(4'b1011), .out(multiplexer_7_out), .sel(and_16_out));
  and and_16 (and_16_out, RType, f3_1, f7_1);
  assign controlled_buffer_1_out = or_4_out ? 4'b0000 : 4'bz;  // Controlled_Buffer controlled_buffer_1
  or or_4 (or_4_out, and_2_out, IType1, and_3_out, UType, IType3, MemRW, SBType, UJType);
  and and_17 (and_17_out, RType, f3_7, f7_0);
  assign controlled_buffer_1_out = or_5_out ? 4'b0010 : 4'bz;  // Controlled_Buffer controlled_buffer_2
  or or_5 (or_5_out, and_4_out, and_5_out);
  assign controlled_buffer_1_out = or_6_out ? 4'b0011 : 4'bz;  // Controlled_Buffer controlled_buffer_3
  or or_6 (or_6_out, and_6_out, and_7_out);
  assign controlled_buffer_1_out = or_7_out ? 4'b0100 : 4'bz;  // Controlled_Buffer controlled_buffer_4
  or or_7 (or_7_out, and_8_out, and_9_out);
  assign controlled_buffer_1_out = or_8_out ? 4'b0110 : 4'bz;  // Controlled_Buffer controlled_buffer_5
  or or_8 (or_8_out, and_10_out, and_11_out);
  assign controlled_buffer_1_out = or_9_out ? 4'b0111 : 4'bz;  // Controlled_Buffer controlled_buffer_6
  or or_9 (or_9_out, and_12_out, and_13_out);
  assign controlled_buffer_1_out = and_18_out ? 4'b1000 : 4'bz;  // Controlled_Buffer controlled_buffer_7
  and and_18 (and_18_out, RType, f3_4, f7_1);
  assign controlled_buffer_1_out = and_19_out ? 4'b1001 : 4'bz;  // Controlled_Buffer controlled_buffer_8
  and and_19 (and_19_out, RType, f3_6, f7_1);
  assign controlled_buffer_1_out = and_20_out ? 4'b1010 : 4'bz;  // Controlled_Buffer controlled_buffer_9
  and and_20 (and_20_out, RType, f3_0, f7_1);
  assign controlled_buffer_1_out = and_21_out ? 4'b1011 : 4'bz;  // Controlled_Buffer controlled_buffer_10
  and and_21 (and_21_out, RType, f3_1, f7_1);
  assign controlled_buffer_1_out = and_22_out ? 4'b1100 : 4'bz;  // Controlled_Buffer controlled_buffer_11
  and and_22 (and_22_out, RType, f3_0, f7_2);
  Comparator #(.width(7)) comparator_1 (.a(opcode), .b(7'b0110011), .eq(RType));  // open: gt, lt
  Comparator #(.width(7)) comparator_2 (.a(opcode), .b(7'b0000011), .eq(IType1));  // open: gt, lt
  Comparator #(.width(7)) comparator_3 (.a(opcode), .b(7'b0010011), .eq(IType2));  // open: gt, lt
  Comparator #(.width(7)) comparator_4 (.a(opcode), .b(7'b0100011), .eq(MemRW));  // open: gt, lt
  Comparator #(.width(7)) comparator_5 (.a(opcode), .b(7'b1100011), .eq(SBType));  // open: gt, lt
  Comparator #(.width(7)) comparator_6 (.a(opcode), .b(7'b0110111), .eq(UType));  // open: gt, lt
  Comparator #(.width(7)) comparator_7 (.a(opcode), .b(7'b1101111), .eq(UJType));  // open: gt, lt
  Comparator #(.width(7)) comparator_8 (.a(opcode), .b(7'b1100111), .eq(IType3));  // open: gt, lt
  or or_10 (PCSel, UJType, IType3, and_14_out, and_15_out);
  Multiplexer #(.width(3), .enable("false")) multiplexer_8 (
    .in0(multiplexer_5_out), .in1(3'b000), .out(ImmSel), .sel(or_11_out));
  or or_11 (or_11_out, RType, IType1, IType2, IType3);
  Multiplexer #(.width(2), .enable("false")) multiplexer_9 (
    .in0(multiplexer_6_out), .in1(2'b00), .out(WBSel), .sel(IType1));
  assign controlled_buffer_1_out = and_17_out ? 4'b0001 : 4'bz;  // Controlled_Buffer controlled_buffer_12
  Multiplexer #(.width(4), .enable("false")) multiplexer_10 (
    .in0(multiplexer_7_out), .in1(4'b1010), .out(multiplexer_10_out), .sel(and_23_out));
  and and_23 (and_23_out, RType, f3_0, f7_1);
  and and_24 (and_24_out, RType, f3_6, f7_1);
  Comparator #(.width(3)) comparator_9 (.a(funct3), .b(3'b000), .eq(f3_0));  // open: gt, lt
  Comparator #(.width(3)) comparator_10 (.a(funct3), .b(3'b001), .eq(f3_1));  // open: gt, lt
  Comparator #(.width(3)) comparator_11 (.a(funct3), .b(3'b010), .eq(f3_2));  // open: gt, lt
  Comparator #(.width(3)) comparator_12 (.a(funct3), .b(3'b100), .eq(f3_4));  // open: gt, lt
  Comparator #(.width(3)) comparator_13 (.a(funct3), .b(3'b101), .eq(f3_5));  // open: gt, lt
  Comparator #(.width(3)) comparator_14 (.a(funct3), .b(3'b110), .eq(f3_6));  // open: gt, lt
  Comparator #(.width(3)) comparator_15 (.a(funct3), .b(3'b111), .eq(f3_7));  // open: gt, lt
  Multiplexer #(.width(4), .enable("false")) multiplexer_11 (
    .in0(multiplexer_10_out), .in1(4'b1001), .out(multiplexer_11_out), .sel(and_24_out));
  or or_12 (or_12_out, MemRW, SBType);
  Multiplexer #(.width(4), .enable("false")) multiplexer_12 (
    .in0(multiplexer_11_out), .in1(4'b1000), .out(multiplexer_12_out), .sel(and_25_out));
  and and_25 (and_25_out, RType, f3_4, f7_1);
  not not_1 (RegWEn, or_12_out);
  and and_26 (BrUn, SBType, f3_6);
  not not_2 (BSel, RType);
  or or_13 (ASel, SBType, UJType);
  and and_27 (and_27_out, RType, f3_2, f7_0);
  or or_14 (or_14_out, and_27_out, and_28_out);
  and and_28 (and_28_out, IType2, f3_2);
  Comparator #(.width(7)) comparator_16 (.a(funct7), .b({7{1'b0}}), .eq(f7_0));  // open: gt, lt
  Comparator #(.width(7)) comparator_17 (.a(funct7), .b(7'b0000001), .eq(f7_1));  // open: gt, lt
  Comparator #(.width(7)) comparator_18 (.a(funct7), .b(7'b0100000), .eq(f7_2));  // open: gt, lt
  Multiplexer #(.width(4), .enable("false")) multiplexer_13 (
    .in0(multiplexer_12_out), .in1(4'b0111), .out(multiplexer_13_out), .sel(or_14_out));
  and and_29 (and_29_out, RType, f3_1, f7_0);
  and and_30 (and_30_out, IType2, f3_1, f7_0);
  assign controlled_buffer_13_out = IType1 ? 2'b00 : 2'bz;  // Controlled_Buffer controlled_buffer_13
  assign controlled_buffer_13_out = or_15_out ? 2'b01 : 2'bz;  // Controlled_Buffer controlled_buffer_14
  or or_15 (or_15_out, RType, IType2, UType);
  assign controlled_buffer_13_out = or_16_out ? 2'b10 : 2'bz;  // Controlled_Buffer controlled_buffer_15
  or or_16 (or_16_out, UJType, IType3);
  Multiplexer #(.width(4), .enable("false")) multiplexer_14 (
    .in0(multiplexer_13_out), .in1(4'b0110), .out(multiplexer_14_out), .sel(or_17_out));
  or or_17 (or_17_out, and_29_out, and_30_out);
  and and_31 (and_31_out, RType, f3_5, f7_0);
  or or_18 (or_18_out, and_31_out, and_32_out);
  and and_32 (and_32_out, IType2, f3_5, f7_0);
  Multiplexer #(.width(4), .enable("false")) multiplexer_15 (
    .in0(multiplexer_14_out), .in1(4'b0100), .out(multiplexer_15_out), .sel(or_18_out));
  and and_33 (and_33_out, RType, f3_4, f7_0);
  and and_34 (and_34_out, IType2, f3_4);
  Multiplexer #(.width(4), .enable("false")) multiplexer_16 (
    .in0(multiplexer_15_out), .in1(4'b0011), .out(multiplexer_16_out), .sel(or_19_out));
  or or_19 (or_19_out, and_33_out, and_34_out);
  and and_35 (and_35_out, RType, f3_6, f7_0);
  and and_36 (and_36_out, IType2, f3_6);
  Multiplexer #(.width(4), .enable("false")) multiplexer_17 (
    .in0(multiplexer_16_out), .in1(4'b0010), .out(multiplexer_17_out), .sel(or_20_out));
  or or_20 (or_20_out, and_35_out, and_36_out);
  Multiplexer #(.width(4), .enable("false")) multiplexer_18 (
    .in0(multiplexer_17_out), .in1(4'b0001), .out(multiplexer_18_out), .sel(and_37_out));
  and and_37 (and_37_out, RType, f3_7, f7_0);
  and and_38 (and_38_out, RType, f3_0, f7_0);
  and and_39 (and_39_out, f3_0, IType2);
  or or_21 (or_21_out, and_38_out, IType1, and_39_out, UType, IType3, MemRW, SBType, UJType);
  Multiplexer #(.width(4), .enable("false")) multiplexer_19 (
    .in0(multiplexer_18_out), .in1(4'b0000), .out(ALUSel), .sel(or_21_out));

  // Other names for the same wires on the sheet: SType = MemRW

  // Notes on the sheet:
  //   Fix the PCSel, has to be determined by the BrEq and BrLT, take them as inputs
endmodule

module BranchComp (
  input  [31:0] rs1,
  input  [31:0] rs2,
  input  BrUn,
  output BrEq,
  output BrLT
);

  wire comparator_1_lt, comparator_2_lt;

  Comparator #(.width(32)) comparator_1 (.a(rs1), .b(rs2), .lt(comparator_1_lt));  // open: gt, eq
  Comparator #(.width(32), .mode("unsigned")) comparator_2 (.a(rs1), .b(rs2), .lt(comparator_2_lt));  // open: gt, eq
  Comparator #(.width(32)) comparator_3 (.a(rs1), .b(rs2), .eq(BrEq));  // open: gt, lt
  Multiplexer #(.enable("false")) multiplexer_1 (.in0(comparator_1_lt), .in1(comparator_2_lt), .out(BrLT), .sel(BrUn));
endmodule

module ImmGen (
  input  [31:0] instruction,
  input  [2:0] ImmSel,
  output [31:0] immediate
);

  wire [31:0] bit_extender_1_out, bit_extender_2_out, bit_extender_3_out, bit_extender_4_out;

  assign bit_extender_1_out = {{20{instruction[31]}}, instruction[31:20]};  // Bit_Extender bit_extender_1
  assign bit_extender_2_out = {{20{instruction[31]}}, {instruction[31:25], instruction[11:7]}};  // Bit_Extender bit_extender_2
  assign bit_extender_3_out = {{11{instruction[31]}}, {instruction[31], instruction[19:12], instruction[20], instruction[30:21], 1'b0}};  // Bit_Extender bit_extender_3
  assign bit_extender_4_out = {{19{instruction[31]}}, {instruction[31], instruction[7], instruction[30:25], instruction[11:8], 1'b0}};  // Bit_Extender bit_extender_4
  Multiplexer #(.select(3), .width(32), .enable("false")) multiplexer_1 (
    .in0(bit_extender_1_out), .in1(bit_extender_2_out), .in2(bit_extender_4_out),
    .in3({instruction[31:12], {12{1'b0}}}), .in4(bit_extender_3_out), .out(immediate), .sel(ImmSel));  // open: in5, in6, in7

  // Notes on the sheet:
  //   SBType
  //   UType
  //   UJType
  //   IType
  //   SType
endmodule
