// Logisim project alu.circ as structural Verilog: 1 circuit, main circuit main
module main (
  input  [31:0] X,
  input  [31:0] Y,
  input  [3:0] Switch,
  output Equal,
  output [31:0] Result
);

  wire comparator_2_lt;
  wire [4:0] bit_extender_2_out, bit_extender_3_out, bit_extender_4_out;
  wire [31:0] add, \and , div, mulh, mult, \or , rem, sll, slt, sra, srl, \xor ;

  Comparator #(.width(32)) comparator_1 (.a(X), .b(Y), .eq(Equal));  // open: gt, lt
  Adder #(.width(32)) adder_1 (.a(X), .b(Y), .out(add));  // open: cin, cout
  Comparator #(.width(32)) comparator_2 (.a(X), .b(Y), .lt(comparator_2_lt));  // open: gt, eq
  Multiplexer #(.select(4), .width(32), .enable("false")) multiplexer_1 (
    .in0(add), .in1(\and ), .in2(\or ), .in3(\xor ), .in4(srl), .in5(sra), .in6(sll), .in7(slt), .in8(div),
    .in9(rem), .in10(mult), .in11(mulh), .out(Result), .sel(Switch));  // open: in12, in13, in14, in15
  assign slt = {{31{1'b0}}, comparator_2_lt};  // Bit_Extender bit_extender_1
  assign \or  = X | Y;  // OR_Gate or_1, 32 bits wide
  assign \xor  = X ^ Y;  // XOR_Gate xor_1, 32 bits wide
  Divider #(.width(32)) divider_1 (.a(X), .b(Y), .out(div));  // open: upper, rem
  Bit_Extender #(.in_width(32), .out_width(5)) bit_extender_2 (.in(Y), .out(bit_extender_2_out));
  Bit_Extender #(.in_width(32), .out_width(5)) bit_extender_3 (.in(Y), .out(bit_extender_3_out));
  Shifter #(.width(32), .shift("lr")) shifter_1 (.in(X), .\dist (bit_extender_2_out), .out(srl));
  Shifter #(.width(32), .shift("ar")) shifter_2 (.in(X), .\dist (bit_extender_3_out), .out(sra));
  assign \and  = X & Y;  // AND_Gate and_1, 32 bits wide
  Bit_Extender #(.in_width(32), .out_width(5)) bit_extender_4 (.in(Y), .out(bit_extender_4_out));
  Shifter #(.width(32)) shifter_3 (.in(X), .\dist (bit_extender_4_out), .out(sll));
  Multiplier #(.width(32)) multiplier_1 (.a(X), .b(Y), .out(mult));  // open: cin, cout
  Multiplier #(.width(32)) multiplier_2 (.a(X), .b(Y), .cout(mulh));  // open: out, cin
  Divider #(.width(32)) divider_2 (.a(X), .b(Y), .rem(rem));  // open: out, upper

  // Other names for the same wires on the sheet: S[3:0] = Switch

  // Notes on the sheet:
  //   INPUTS to your circuit
  //   DON'T CHANGE THE LOCATIONS OF THE INPUTS AND OUTPUTS!
  //   OUTPUTS from your circuit
endmodule
