// Logisim project cpu.circ as structural Verilog: 5 circuits, main circuit main
module main (
  input  [31:0] INSTRUCTION,
  input  CLOCK,
  output [31:0] FETCH_ADDRESS,
  output [31:0] ra_Value,
  output [31:0] sp_Value,
  output [31:0] t0_Value,
  output [31:0] t1_Value,
  output [31:0] t2_Value,
  output [31:0] s0_Value,
  output [31:0] s1_Value,
  output [31:0] a0_Value
);

  wire ASel, BrEq, BrLT, BRUn, BSel, control_unit_1_luisel, control_unit_1_negsel, control_unit_1_swge,
       MemRW, PCSel, RegWEn;
  wire [1:0] WBSel;
  wire [2:0] Func3, ImmSel;
  wire [3:0] ALUSel;
  wire [4:0] rd, rs1, rs2;
  wire [6:0] Func7, OpCode;
  wire [31:0] alu, ImmGen, main_3_read_data, multiplexer_1_out, multiplexer_2_out, multiplexer_3_out, PC,
       PC_4, R1, R2, wb;

  Shifter #(.width(32), .shift("lr")) shifter_1 (.in(PC), .\dist (5'b00010), .out(FETCH_ADDRESS));
  Adder #(.width(32)) adder_1 (.a(PC), .b(32'h4), .out(PC_4));  // open: cin, cout
  Register #(.width(32)) u_PC (.D(multiplexer_1_out), .Q(PC), .clk(CLOCK));  // open: en, clr
  Multiplexer #(.width(32), .enable("false")) multiplexer_1 (
    .in0(PC_4), .in1(alu), .out(multiplexer_1_out), .sel(PCSel));
  Immediate_Generator immediate_generator_1 (.instruction(INSTRUCTION), .ImmSel(ImmSel), .immediate(ImmGen));
  Branch_Comparator branch_comparator_1 (.RS1(R1), .BrUn(BRUn), .RS2(R2), .BrEq(BrEq), .BrLt(BrLT));
  Split_Instruction split_instruction_1 (
    .Instruction(INSTRUCTION), .OpCode(OpCode), .rd(rd), .Func3(Func3), .rs1(rs1), .rs2(rs2), .Func7(Func7));
  Control_Unit control_unit_1 (
    .OpCode(OpCode), .Func3(Func3), .BrEq(BrEq), .Func7(Func7), .BrLT(BrLT), .PCSel(PCSel), .ImmSel(ImmSel),
    .RegWEn(RegWEn), .BrUn(BRUn), .BSel(BSel), .ASel(ASel), .ALUSel(ALUSel), .MemRW(MemRW), .WBSel(WBSel),
    .NegSel(control_unit_1_negsel), .LuiSel(control_unit_1_luisel), .SWGE(control_unit_1_swge));
  // Probe on ra_Value
  // Probe on sp_Value
  regfile_main main_1 (
    .Read_Register_1__rs1(rs1), .Read_Register_2__rs2(rs2), .Write_Register__rd(rd), .Write_Data(wb),
    .Write_Enable(RegWEn), .Clock(CLOCK), .Read_Data_1(R1), .Read_Data_2(R2), .ra_Value(ra_Value),
    .sp_Value(sp_Value), .t0_Value(t0_Value), .t1_Value(t1_Value), .t2_Value(t2_Value), .s0_Value(s0_Value),
    .s1_Value(s1_Value), .a0_Value(a0_Value));
  // Probe on t0_Value
  // Probe on t1_Value
  Multiplexer #(.width(32), .enable("false")) multiplexer_2 (.in0(R1), .in1(PC), .out(multiplexer_2_out), .sel(ASel));
  Multiplexer #(.width(32), .enable("false")) multiplexer_3 (
    .in0(R2), .in1(ImmGen), .out(multiplexer_3_out), .sel(BSel));
  // Probe on t2_Value
  // Probe on s0_Value
  // Probe on s1_Value
  alu_main main_2 (.Switch(ALUSel), .X(multiplexer_2_out), .Result(alu), .Y(multiplexer_3_out));  // open: Equal
  // Probe on a0_Value
  mem_main main_3 (.Address(alu), .Write_Data(R2), .Write_En(MemRW), .Clock(CLOCK), .Read_Data(main_3_read_data));
  Multiplexer #(.select(2), .width(32), .enable("false")) multiplexer_4 (
    .in0(main_3_read_data), .in1(alu), .in2(PC_4), .out(wb), .sel(WBSel));  // open: in3

  // Other names for the same wires on the sheet: a0[31:0] = a0_Value; clk = CLOCK; fetch_addr[31:0] = FETCH_ADDRESS;
  //   Input[31:0] = INSTRUCTION; ra[31:0] = ra_Value; s0[31:0] = s0_Value; s1[31:0] = s1_Value; sp[31:0] = sp_Value;
  //   t0[31:0] = t0_Value; t1[31:0] = t1_Value; t2[31:0] = t2_Value

  // Notes on the sheet:
  //   Output
  //   These are outputs/inputs from run.circ
  //   Inputs
endmodule

module Split_Instruction (
  input  [31:0] Instruction,
  output [6:0] OpCode,
  output [4:0] rd,
  output [2:0] Func3,
  output [4:0] rs1,
  output [4:0] rs2,
  output [6:0] Func7
);


  assign Func3 = Instruction[14:12];
  assign Func7 = Instruction[31:25];
  assign OpCode = Instruction[6:0];
  assign rd = Instruction[11:7];
  assign rs1 = Instruction[19:15];
  assign rs2 = Instruction[24:20];
endmodule

module Control_Unit (
  input  [6:0] OpCode,
  input  [2:0] Func3,
  input  BrEq,
  input  [6:0] Func7,
  input  BrLT,
  output PCSel,
  output [2:0] ImmSel,
  output RegWEn,
  output BrUn,
  output BSel,
  output ASel,
  output [3:0] ALUSel,
  output MemRW,
  output [1:0] WBSel,
  output NegSel,
  output LuiSel,
  output SWGE
);

  wire add, addi, \and , and_16_out, and_17_out, andi, beq, blt, div, Func3_0, Func3_1, Func3_2, Func3_4,
       Func3_5, Func3_6, Func3_7, Func7_00, Func7_01, Func7_20, I_Type, I_Type_03, I_Type_13, I_Type_67, jal,
       jalr, lb, lh, lw, mul, mulh, \or , or_3_out, or_4_out, or_5_out, or_6_out, or_7_out, or_8_out,
       or_9_out, or_11_out, or_12_out, or_13_out, ori, R_Type, rem, S_Type, SB_Type, sll, slli, slt, slti,
       srl, srli, \xor , xori;
  wire [1:0] multiplexer_12_out, multiplexer_13_out;
  wire [2:0] multiplexer_11_out, multiplexer_14_out, multiplexer_16_out;
  wire [3:0] multiplexer_1_out, multiplexer_2_out, multiplexer_3_out, multiplexer_4_out, multiplexer_5_out,
       multiplexer_7_out, multiplexer_8_out, multiplexer_9_out, multiplexer_10_out;

  Comparator #(.width(7)) comparator_1 (.a(OpCode), .b(7'b0110011), .eq(R_Type));  // open: gt, lt
  Comparator #(.width(7)) comparator_2 (.a(OpCode), .b(7'b0000011), .eq(I_Type_03));  // open: gt, lt
  Comparator #(.width(7)) comparator_3 (.a(OpCode), .b(7'b0010011), .eq(I_Type_13));  // open: gt, lt
  Comparator #(.width(7)) comparator_4 (.a(OpCode), .b(7'b1100111), .eq(I_Type_67));  // open: gt, lt
  Comparator #(.width(7)) comparator_5 (.a(OpCode), .b(7'b0100011), .eq(S_Type));  // open: gt, lt
  Comparator #(.width(7)) comparator_6 (.a(OpCode), .b(7'b1100011), .eq(SB_Type));  // open: gt, lt
  Comparator #(.width(7)) comparator_7 (.a(OpCode), .b(7'b1101111), .eq(jal));  // open: gt, lt
  Comparator #(.width(7)) comparator_8 (.a(OpCode), .b(7'b0110111), .eq(LuiSel));  // open: gt, lt
  or or_1 (I_Type, I_Type_03, I_Type_13, I_Type_67);
  not not_1 (BSel, R_Type);
  nor nor_1 (RegWEn, S_Type, SB_Type);
  or or_2 (ASel, SB_Type, jal);
  or or_3 (or_3_out, slt, slti);
  or or_4 (or_4_out, srl, srli);
  or or_5 (or_5_out, \or , ori);
  or or_6 (or_6_out, blt, BrUn);
  Multiplexer #(.width(4), .enable("false")) multiplexer_1 (
    .in0(multiplexer_2_out), .in1(4'b0110), .out(multiplexer_1_out), .sel(or_7_out));
  or or_7 (or_7_out, sll, slli);
  Multiplexer #(.width(4), .enable("false")) multiplexer_2 (
    .in0(multiplexer_3_out), .in1(4'b0100), .out(multiplexer_2_out), .sel(or_4_out));
  Multiplexer #(.width(4), .enable("false")) multiplexer_3 (
    .in0(multiplexer_4_out), .in1(4'b0011), .out(multiplexer_3_out), .sel(or_8_out));
  or or_8 (or_8_out, \xor , xori);
  Multiplexer #(.width(4), .enable("false")) multiplexer_4 (
    .in0(multiplexer_5_out), .in1(4'b0010), .out(multiplexer_4_out), .sel(or_5_out));
  Multiplexer #(.width(4), .enable("false")) multiplexer_5 (
    .in0(4'b0000), .in1(4'b0001), .out(multiplexer_5_out), .sel(or_9_out));
  or or_9 (or_9_out, \and , andi);
  Comparator #(.width(3)) comparator_9 (.a(Func3), .b(3'b000), .eq(Func3_0));  // open: gt, lt
  Comparator #(.width(3)) comparator_10 (.a(Func3), .b(3'b001), .eq(Func3_1));  // open: gt, lt
  Comparator #(.width(3)) comparator_11 (.a(Func3), .b(3'b010), .eq(Func3_2));  // open: gt, lt
  Comparator #(.width(3)) comparator_12 (.a(Func3), .b(3'b100), .eq(Func3_4));  // open: gt, lt
  Comparator #(.width(3)) comparator_13 (.a(Func3), .b(3'b101), .eq(Func3_5));  // open: gt, lt
  Comparator #(.width(3)) comparator_14 (.a(Func3), .b(3'b110), .eq(Func3_6));  // open: gt, lt
  Comparator #(.width(3)) comparator_15 (.a(Func3), .b(3'b111), .eq(Func3_7));  // open: gt, lt
  and and_1 (add, R_Type, Func7_00, Func3_0);
  and and_2 (mul, R_Type, Func7_01, Func3_0);
  and and_3 (NegSel, R_Type, Func7_20, Func3_0);
  and and_4 (sll, R_Type, Func7_00, Func3_1);
  and and_5 (mulh, R_Type, Func7_01, Func3_1);
  and and_6 (slt, R_Type, Func7_00, Func3_2);
  and and_7 (lb, I_Type_03, Func3_0);
  and and_8 (lh, I_Type_03, Func3_1);
  and and_9 (lw, I_Type_03, Func3_2);
  and and_10 (addi, I_Type_13, Func3_0);
  and and_11 (slli, I_Type_13, Func7_00, Func3_1);
  and and_12 (jalr, I_Type_67, Func3_2);
  and and_13 (MemRW, S_Type, Func3_2);
  and and_14 (beq, SB_Type, Func3_0);
  and and_15 (blt, SB_Type, Func3_4);
  and and_16 (and_16_out, BrEq, beq);
  and and_17 (and_17_out, BrLT, or_6_out);
  Multiplexer #(.width(4), .enable("false")) multiplexer_6 (
    .in0(multiplexer_7_out), .in1(4'b1011), .out(ALUSel), .sel(mulh));
  Multiplexer #(.width(4), .enable("false")) multiplexer_7 (
    .in0(multiplexer_8_out), .in1(4'b1010), .out(multiplexer_7_out), .sel(mul));
  Multiplexer #(.width(4), .enable("false")) multiplexer_8 (
    .in0(multiplexer_9_out), .in1(4'b1001), .out(multiplexer_8_out), .sel(rem));
  Multiplexer #(.width(4), .enable("false")) multiplexer_9 (
    .in0(multiplexer_10_out), .in1(4'b1000), .out(multiplexer_9_out), .sel(div));
  Multiplexer #(.width(4), .enable("false")) multiplexer_10 (
    .in0(multiplexer_1_out), .in1(4'b0111), .out(multiplexer_10_out), .sel(or_3_out));
  or or_10 (PCSel, and_16_out, jal, I_Type_67, and_17_out);
  or or_11 (or_11_out, LuiSel, I_Type_67);
  Multiplexer #(.width(3), .enable("false")) multiplexer_11 (
    .in0(3'b100), .in1(3'b011), .out(multiplexer_11_out), .sel(LuiSel));
  Comparator #(.width(7)) comparator_16 (.a(Func7), .b({7{1'b0}}), .eq(Func7_00));  // open: gt, lt
  Comparator #(.width(7)) comparator_17 (.a(Func7), .b(7'b0000001), .eq(Func7_01));  // open: gt, lt
  Comparator #(.width(7)) comparator_18 (.a(Func7), .b(7'b0100000), .eq(Func7_20));  // open: gt, lt
  and and_18 (\xor , R_Type, Func7_00, Func3_4);
  and and_19 (div, R_Type, Func7_01, Func3_4);
  and and_20 (srl, R_Type, Func7_00, Func3_5);
  and and_21 (\or , R_Type, Func7_00, Func3_6);
  and and_22 (rem, R_Type, Func7_01, Func3_6);
  and and_23 (\and , R_Type, Func7_00, Func3_7);
  and and_24 (slti, I_Type_13, Func3_2);
  and and_25 (xori, I_Type_13, Func3_4);
  and and_26 (srli, I_Type_13, Func7_00, Func3_5);
  and and_27 (ori, I_Type_13, Func3_6);
  and and_28 (andi, I_Type_13, Func3_7);
  and and_29 (SWGE, S_Type, Func3_7);
  and and_30 (BrUn, SB_Type, Func3_6);
  Multiplexer #(.width(2), .enable("false")) multiplexer_12 (
    .in0(2'b00), .in1(2'b10), .out(multiplexer_12_out), .sel(or_11_out));
  Multiplexer #(.width(2), .enable("false")) multiplexer_13 (
    .in0(multiplexer_12_out), .in1(2'b01), .out(multiplexer_13_out), .sel(or_12_out));
  or or_12 (or_12_out, R_Type, LuiSel, I_Type_13);
  Multiplexer #(.width(3), .enable("false")) multiplexer_14 (
    .in0(multiplexer_11_out), .in1(3'b010), .out(multiplexer_14_out), .sel(SB_Type));
  Multiplexer #(.width(2), .enable("false")) multiplexer_15 (
    .in0(multiplexer_13_out), .in1(2'b00), .out(WBSel), .sel(I_Type_03));
  Multiplexer #(.width(3), .enable("false")) multiplexer_16 (
    .in0(multiplexer_14_out), .in1(3'b001), .out(multiplexer_16_out), .sel(S_Type));
  Multiplexer #(.width(3), .enable("false")) multiplexer_17 (
    .in0(multiplexer_16_out), .in1(3'b000), .out(ImmSel), .sel(or_13_out));
  or or_13 (or_13_out, R_Type, I_Type);

  // Other names for the same wires on the sheet: bltu = BrUn; UJ_Type = jal; lui = LuiSel; U_Type = LuiSel;
  //   sub = NegSel; sw = MemRW
endmodule

module Branch_Comparator (
  input  [31:0] RS1,
  input  BrUn,
  input  [31:0] RS2,
  output BrEq,
  output BrLt
);

  wire comparator_1_lt, comparator_2_lt;

  Comparator #(.width(32)) comparator_1 (.a(RS1), .b(RS2), .eq(BrEq), .lt(comparator_1_lt));  // open: gt
  Comparator #(.width(32), .mode("unsigned")) comparator_2 (.a(RS1), .b(RS2), .lt(comparator_2_lt));  // open: gt, eq
  Multiplexer #(.enable("false")) multiplexer_1 (.in0(comparator_1_lt), .in1(comparator_2_lt), .out(BrLt), .sel(BrUn));
endmodule

module Immediate_Generator (
  input  [31:0] instruction,
  input  [2:0] ImmSel,
  output [31:0] immediate
);

  wire [31:0] bit_extender_1_out, bit_extender_2_out, bit_extender_3_out, bit_extender_4_out;

  assign bit_extender_1_out = {{19{instruction[31]}}, {instruction[31], instruction[7], instruction[30:25], instruction[11:8], 1'b0}};  // Bit_Extender bit_extender_1
  assign bit_extender_2_out = {{11{instruction[31]}}, {instruction[31], instruction[19:12], instruction[20], instruction[30:21], 1'b0}};  // Bit_Extender bit_extender_2
  assign bit_extender_3_out = {{20{instruction[31]}}, instruction[31:20]};  // Bit_Extender bit_extender_3
  assign bit_extender_4_out = {{20{instruction[31]}}, {instruction[31:25], instruction[11:7]}};  // Bit_Extender bit_extender_4
  Multiplexer #(.select(3), .width(32), .enable("false")) multiplexer_1 (
    .in0(bit_extender_3_out), .in1(bit_extender_4_out), .in2(bit_extender_1_out),
    .in3({instruction[31:12], {12{1'b0}}}), .in4(bit_extender_2_out), .out(immediate), .sel(ImmSel));  // open: in5, in6, in7

  // Notes on the sheet:
  //   SBType
  //   UType
  //   UJType
  //   SType
  //   IType
endmodule
