// Logisim project vedcpu.circ as structural Verilog: 4 circuits, main circuit main
module main (
  input  [31:0] INSTRUCTION,
  input  CLOCK,
  output [31:0] FETCH_ADDRESS,
  output [31:0] ra_Value,
  output [31:0] sp_Value,
  output [31:0] t0_Value,
  output [31:0] t1_Value,
  output [31:0] t2_Value,
  output [31:0] s0_Value,
  output [31:0] s1_Value,
  output [31:0] a0_Value
);

  wire and_1_out, ASel, BrEq, BrLt, BrUn, BSel, comparator_1_eq, comparator_1_gt, LuiSel, MemRW, NegSel,
       or_1_out, or_2_out, PCSel, RegWEn, SWGE;
  wire [1:0] WBSel;
  wire [2:0] ImmSel;
  wire [3:0] ALUSel;
  wire [31:0] alu, ImmGen, MEM_read_data, multiplexer_1_out, multiplexer_2_out, multiplexer_3_out,
       multiplexer_4_out, multiplexer_5_out, negator_1_out, PC, PC_4, R1, R2, wb;

  Shifter #(.width(32), .shift("lr")) shifter_1 (.in(PC), .\dist (5'b00010), .out(FETCH_ADDRESS));
  Multiplexer #(.width(32), .disabled(0), .enable("false")) multiplexer_1 (
    .in0(PC_4), .in1(alu), .out(multiplexer_1_out), .sel(PCSel));
  // Probe on ra_Value
  Adder #(.width(32)) adder_1 (.a(PC), .b(32'h4), .out(PC_4));  // open: cin, cout
  Register #(.width(32)) u_PC (.D(multiplexer_1_out), .Q(PC), .clk(CLOCK));  // open: en, clr
  // Probe on sp_Value
  // Probe on t0_Value
  // Probe on t1_Value
  // Probe on t2_Value
  regfile_main main_1 (
    .Read_Register_1__rs1(INSTRUCTION[19:15]), .Read_Register_2__rs2(INSTRUCTION[24:20]),
    .Write_Register__rd(INSTRUCTION[11:7]), .Write_Data(wb), .Write_Enable(RegWEn), .Clock(CLOCK),
    .Read_Data_1(R1), .Read_Data_2(R2), .ra_Value(ra_Value), .sp_Value(sp_Value), .t0_Value(t0_Value),
    .t1_Value(t1_Value), .t2_Value(t2_Value), .s0_Value(s0_Value), .s1_Value(s1_Value), .a0_Value(a0_Value));
  // Probe on s0_Value
  // Probe on s1_Value
  Multiplexer #(.width(32), .disabled(0), .enable("false")) multiplexer_2 (
    .in0(R1), .in1(PC), .out(multiplexer_2_out), .sel(ASel));
  Multiplexer #(.width(32), .disabled(0), .enable("false")) multiplexer_3 (
    .in0(R2), .in1(ImmGen), .out(multiplexer_3_out), .sel(BSel));
  Comparator #(.width(32)) comparator_1 (.a(R2), .b(ImmGen), .gt(comparator_1_gt), .eq(comparator_1_eq));  // open: lt
  // Probe on a0_Value
  Multiplexer #(.width(32), .disabled(0), .enable("false")) multiplexer_4 (
    .in0(multiplexer_3_out), .in1(negator_1_out), .out(multiplexer_4_out), .sel(NegSel));
  Negator #(.width(32)) negator_1 (.in(multiplexer_3_out), .out(negator_1_out));
  or or_1 (or_1_out, comparator_1_gt, comparator_1_eq);
  Immediate_Generator Imm__Gen (.Instruction(INSTRUCTION), .ImmSel(ImmSel), .ImmGen(ImmGen));
  Branch_Comparator Branch_Comparator (.RS1(R1), .BrUn(BrUn), .RS2(R2), .BrEq(BrEq), .BrLt(BrLt));
  Multiplexer #(.width(32), .disabled(0), .enable("false")) multiplexer_5 (
    .in0(multiplexer_2_out), .in1({32{1'b0}}), .out(multiplexer_5_out), .sel(LuiSel));
  alu_main main_2 (.Switch(ALUSel), .X(multiplexer_5_out), .Result(alu), .Y(multiplexer_4_out));  // open: Equal
  and and_1 (and_1_out, or_1_out, SWGE);
  or or_2 (or_2_out, and_1_out, MemRW);
  Control_Unit control_unit_1 (
    .Instruction(INSTRUCTION), .BrEQ(BrEq), .BrLT(BrLt), .PCSel(PCSel), .ImmSel(ImmSel), .RegWEn(RegWEn),
    .BrUn(BrUn), .BSel(BSel), .ASel(ASel), .ALUSel(ALUSel), .MemRW(MemRW), .WBSel(WBSel), .NegSel(NegSel),
    .LuiSel(LuiSel), .SWGE(SWGE));
  mem_main MEM (.Address(alu), .Write_Data(R2), .Write_En(or_2_out), .Clock(CLOCK), .Read_Data(MEM_read_data));
  Multiplexer #(.select(2), .width(32), .enable("false")) multiplexer_6 (
    .in0(MEM_read_data), .in1(alu), .in2(PC_4), .out(wb), .sel(WBSel));  // open: in3

  // Other names for the same wires on the sheet: a0[31:0] = a0_Value; clk = CLOCK; fetch_addr[31:0] = FETCH_ADDRESS;
  //   Input[31:0] = INSTRUCTION; rd[4:0] = INSTRUCTION[11:7]; rs1[4:0] = INSTRUCTION[19:15];
  //   rs2[4:0] = INSTRUCTION[24:20]; ra[31:0] = ra_Value; s0[31:0] = s0_Value; s1[31:0] = s1_Value;
  //   sp[31:0] = sp_Value; t0[31:0] = t0_Value; t1[31:0] = t1_Value; t2[31:0] = t2_Value

  // Notes on the sheet:
  //   Output
  //   These are outputs/inputs from run.circ
  //   Inputs
endmodule

module Branch_Comparator (
  input  [31:0] RS1,
  input  BrUn,
  input  [31:0] RS2,
  output BrEq,
  output BrLt
);

  wire comparator_1_lt, comparator_2_lt;

  Comparator #(.width(32)) comparator_1 (.a(RS1), .b(RS2), .eq(BrEq), .lt(comparator_1_lt));  // open: gt
  Comparator #(.width(32), .mode("unsigned")) comparator_2 (.a(RS1), .b(RS2), .lt(comparator_2_lt));  // open: gt, eq
  Multiplexer #(.enable("false")) multiplexer_1 (.in0(comparator_1_lt), .in1(comparator_2_lt), .out(BrLt), .sel(BrUn));
endmodule

module Control_Unit (
  input  [31:0] Instruction,
  input  BrEQ,
  input  BrLT,
  output PCSel,
  output [2:0] ImmSel,
  output RegWEn,
  output BrUn,
  output BSel,
  output ASel,
  output [3:0] ALUSel,
  output MemRW,
  output [1:0] WBSel,
  output NegSel,
  output LuiSel,
  output SWGE
);

  wire add, addi, \and , and_1_out, and_2_out, andi, beq, blt, bltu, Branch, BrEq_t, BrLt_t, div, Func3_0,
       Func3_1, Func3_2, Func3_3, Func3_4, Func3_5, Func3_6, Func3_7, Func7_00, Func7_01, Func7_20, I_Type,
       I_Type_03, I_Type_13, I_Type_67, isBranch, isJump, jal, jalr, Jump, lb, lh, lw, mul, mulh, \or ,
       or_6_out, or_7_out, or_8_out, or_9_out, or_10_out, or_11_out, or_12_out, or_14_out, ori, R_Type, rem,
       S_Type, SB_Type, sll, slli, slt, slti, srl, srli, \xor , xori;
  wire [1:0] multiplexer_13_out;
  wire [2:0] multiplexer_11_out, multiplexer_12_out, multiplexer_14_out;
  wire [3:0] multiplexer_1_out, multiplexer_2_out, multiplexer_3_out, multiplexer_4_out, multiplexer_5_out,
       multiplexer_6_out, multiplexer_8_out, multiplexer_9_out, multiplexer_10_out;

  // Probe on isBranch
  // Probe on isJump
  Comparator #(.width(7)) comparator_1 (.a(Instruction[6:0]), .b(7'b0110011), .eq(R_Type));  // open: gt, lt
  Comparator #(.width(7)) comparator_2 (.a(Instruction[6:0]), .b(7'b0000011), .eq(I_Type_03));  // open: gt, lt
  Comparator #(.width(7)) comparator_3 (.a(Instruction[6:0]), .b(7'b0010011), .eq(I_Type_13));  // open: gt, lt
  Comparator #(.width(7)) comparator_4 (.a(Instruction[6:0]), .b(7'b1100111), .eq(I_Type_67));  // open: gt, lt
  Comparator #(.width(7)) comparator_5 (.a(Instruction[6:0]), .b(7'b0100011), .eq(S_Type));  // open: gt, lt
  Comparator #(.width(7)) comparator_6 (.a(Instruction[6:0]), .b(7'b1100011), .eq(SB_Type));  // open: gt, lt
  Comparator #(.width(7)) comparator_7 (.a(Instruction[6:0]), .b(7'b1101111), .eq(jal));  // open: gt, lt
  Comparator #(.width(7)) comparator_8 (.a(Instruction[6:0]), .b(7'b0110111), .eq(LuiSel));  // open: gt, lt
  or or_1 (I_Type, I_Type_03, I_Type_13, I_Type_67);
  not not_1 (BSel, R_Type);
  or or_2 (RegWEn, R_Type, I_Type, LuiSel, jal);
  or or_3 (Branch, beq, blt, bltu);
  or or_4 (Jump, jal, jalr);
  or or_5 (ASel, Branch, jal);
  or or_6 (or_6_out, \or , ori);
  or or_7 (or_7_out, blt, bltu);
  or or_8 (or_8_out, slt, slti);
  or or_9 (or_9_out, srl, srli);
  or or_10 (or_10_out, \and , andi);
  and and_1 (and_1_out, BrEq_t, Branch, beq);
  and and_2 (and_2_out, BrLt_t, Branch, or_7_out);
  Multiplexer #(.width(4), .enable("false")) multiplexer_1 (
    .in0(multiplexer_2_out), .in1(4'b0111), .out(multiplexer_1_out), .sel(or_8_out));
  Multiplexer #(.width(4), .enable("false")) multiplexer_2 (
    .in0(multiplexer_3_out), .in1(4'b0110), .out(multiplexer_2_out), .sel(or_11_out));
  or or_11 (or_11_out, sll, slli);
  Multiplexer #(.width(4), .enable("false")) multiplexer_3 (
    .in0(multiplexer_4_out), .in1(4'b0100), .out(multiplexer_3_out), .sel(or_9_out));
  Multiplexer #(.width(4), .enable("false")) multiplexer_4 (
    .in0(multiplexer_5_out), .in1(4'b0011), .out(multiplexer_4_out), .sel(or_12_out));
  or or_12 (or_12_out, \xor , xori);
  Multiplexer #(.width(4), .enable("false")) multiplexer_5 (
    .in0(multiplexer_6_out), .in1(4'b0010), .out(multiplexer_5_out), .sel(or_6_out));
  Multiplexer #(.width(4), .enable("false")) multiplexer_6 (
    .in0(4'b0000), .in1(4'b0001), .out(multiplexer_6_out), .sel(or_10_out));
  Comparator #(.width(3)) comparator_9 (.a(Instruction[14:12]), .b(3'b000), .eq(Func3_0));  // open: gt, lt
  Comparator #(.width(3)) comparator_10 (.a(Instruction[14:12]), .b(3'b001), .eq(Func3_1));  // open: gt, lt
  Comparator #(.width(3)) comparator_11 (.a(Instruction[14:12]), .b(3'b010), .eq(Func3_2));  // open: gt, lt
  Comparator #(.width(3)) comparator_12 (.a(Instruction[14:12]), .b(3'b100), .eq(Func3_4));  // open: gt, lt
  Comparator #(.width(3)) comparator_13 (.a(Instruction[14:12]), .b(3'b101), .eq(Func3_5));  // open: gt, lt
  Comparator #(.width(3)) comparator_14 (.a(Instruction[14:12]), .b(3'b110), .eq(Func3_6));  // open: gt, lt
  Comparator #(.width(3)) comparator_15 (.a(Instruction[14:12]), .b(3'b111), .eq(Func3_7));  // open: gt, lt
  and and_3 (add, R_Type, Func7_00, Func3_0);
  and and_4 (mul, R_Type, Func7_01, Func3_0);
  and and_5 (NegSel, R_Type, Func7_20, Func3_0);
  and and_6 (sll, R_Type, Func7_00, Func3_1);
  and and_7 (mulh, R_Type, Func7_01, Func3_1);
  and and_8 (slt, R_Type, Func7_00, Func3_2);
  and and_9 (lb, I_Type_03, Func3_0);
  and and_10 (lh, I_Type_03, Func3_1);
  and and_11 (lw, I_Type_03, Func3_2);
  and and_12 (addi, I_Type_13, Func3_0);
  and and_13 (slli, I_Type_13, Func7_00, Func3_1);
  and and_14 (jalr, I_Type_67, Func3_2);
  and and_15 (MemRW, S_Type, Func3_2);
  and and_16 (beq, SB_Type, Func3_0);
  and and_17 (blt, SB_Type, Func3_4);
  or or_13 (PCSel, and_1_out, and_2_out, Jump);
  Multiplexer #(.width(4), .enable("false")) multiplexer_7 (
    .in0(multiplexer_8_out), .in1(4'b1011), .out(ALUSel), .sel(mulh));
  Multiplexer #(.width(4), .enable("false")) multiplexer_8 (
    .in0(multiplexer_9_out), .in1(4'b1010), .out(multiplexer_8_out), .sel(mul));
  Multiplexer #(.width(4), .enable("false")) multiplexer_9 (
    .in0(multiplexer_10_out), .in1(4'b1001), .out(multiplexer_9_out), .sel(rem));
  Multiplexer #(.width(4), .enable("false")) multiplexer_10 (
    .in0(multiplexer_1_out), .in1(4'b1000), .out(multiplexer_10_out), .sel(div));
  // Probe on Instruction[6:0]
  Multiplexer #(.width(3), .enable("false")) multiplexer_11 (
    .in0(3'b100), .in1(3'b011), .out(multiplexer_11_out), .sel(LuiSel));
  Multiplexer #(.width(3), .enable("false")) multiplexer_12 (
    .in0(multiplexer_11_out), .in1(3'b010), .out(multiplexer_12_out), .sel(SB_Type));
  // Probe on Instruction[14:12]
  Comparator #(.width(7)) comparator_16 (.a(Instruction[31:25]), .b({7{1'b0}}), .eq(Func7_00));  // open: gt, lt
  Comparator #(.width(7)) comparator_17 (.a(Instruction[31:25]), .b(7'b0000001), .eq(Func7_01));  // open: gt, lt
  Comparator #(.width(7)) comparator_18 (.a(Instruction[31:25]), .b(7'b0100000), .eq(Func7_20));  // open: gt, lt
  and and_18 (\xor , R_Type, Func7_00, Func3_4);
  and and_19 (div, R_Type, Func7_01, Func3_4);
  and and_20 (srl, R_Type, Func7_00, Func3_5);
  and and_21 (\or , R_Type, Func7_00, Func3_6);
  and and_22 (rem, R_Type, Func7_01, Func3_6);
  and and_23 (\and , R_Type, Func7_00, Func3_7);
  and and_24 (slti, I_Type_13, Func3_3);
  and and_25 (xori, I_Type_13, Func3_4);
  and and_26 (srli, I_Type_13, Func7_00, Func3_5);
  and and_27 (ori, I_Type_13, Func3_6);
  and and_28 (andi, I_Type_13, Func3_7);
  and and_29 (SWGE, S_Type, Func3_7);
  and and_30 (bltu, SB_Type, Func3_6);
  Multiplexer #(.width(2), .enable("false")) multiplexer_13 (
    .in0(2'b00), .in1(2'b10), .out(multiplexer_13_out), .sel(Jump));
  Multiplexer #(.width(3), .enable("false")) multiplexer_14 (
    .in0(multiplexer_12_out), .in1(3'b001), .out(multiplexer_14_out), .sel(S_Type));
  // Probe on Instruction[31:25]
  Multiplexer #(.width(2), .enable("false")) multiplexer_15 (
    .in0(multiplexer_13_out), .in1(2'b01), .out(WBSel), .sel(or_14_out));
  or or_14 (or_14_out, R_Type, LuiSel, I_Type_13);
  Multiplexer #(.width(3), .enable("false")) multiplexer_16 (
    .in0(multiplexer_14_out), .in1(3'b000), .out(ImmSel), .sel(I_Type));

  // Other names for the same wires on the sheet: BrUN_t = bltu; OpCode[6:0] = Instruction[6:0];
  //   Func3[2:0] = Instruction[14:12]; Func7[6:0] = Instruction[31:25]; UJ_Type = jal; lui = LuiSel; U_Type = LuiSel;
  //   sub = NegSel; sw = MemRW
endmodule

module Immediate_Generator (
  input  [31:0] Instruction,
  input  [2:0] ImmSel,
  output [31:0] ImmGen
);

  wire [31:0] bit_extender_1_out, bit_extender_2_out, bit_extender_4_out, undriven;

  assign bit_extender_1_out = {{20{Instruction[31]}}, Instruction[31:20]};  // Bit_Extender bit_extender_1
  assign bit_extender_2_out = {{20{Instruction[31]}}, {Instruction[31:25], Instruction[11:7]}};  // Bit_Extender bit_extender_2
  Bit_Extender #(.in_width(13), .out_width(32), .\type ("sign")) bit_extender_3 (.in({Instruction[31], Instruction[7], Instruction[30:25], Instruction[11:8], 1'b0}));  // open: out
  assign bit_extender_4_out = {{11{Instruction[31]}}, {Instruction[31], Instruction[19:12], Instruction[20], Instruction[30:21], 1'b0}};  // Bit_Extender bit_extender_4
  Multiplexer #(.select(3), .width(32), .enable("false")) multiplexer_1 (
    .in0(bit_extender_1_out), .in1(bit_extender_2_out), .in2(undriven),
    .in3({Instruction[31:12], {12{1'b0}}}), .in4(bit_extender_4_out), .out(ImmGen), .sel(ImmSel));  // open: in5, in6, in7

  // Other names for the same wires on the sheet: S_Type_Imm[11:0] = {Instruction[31:25], Instruction[11:7]};
  //   SB_Type_Imm[12:1] = {Instruction[31], Instruction[7], Instruction[30:25], Instruction[11:8]};
  //   I_Type_Imm[11:0] = Instruction[31:20]; U_Type_Imm[31:12] = Instruction[31:12];
  //   UJ_Type_Imm[20:1] = {Instruction[31], Instruction[19:12], Instruction[20], Instruction[30:21]}
endmodule
