// Logisim project regfile-harness.circ as structural Verilog: 1 circuit, main circuit main
module main (
  output [7:0] test_num,
  output [31:0] ra_Value,
  output [31:0] sp_Value,
  output [31:0] t0_Value,
  output [31:0] t1_Value,
  output [31:0] t2_Value,
  output [31:0] s0_Value,
  output [31:0] s1_Value,
  output [31:0] a0_Value,
  output [31:0] Read_Data_1,
  output [31:0] Read_Data_2
);

  wire clock_1_out;
  wire [7:0] adder_1_out;
  wire [15:0] rom_2_data;
  wire [31:0] WriteData;

  Register register_1 (.D(adder_1_out), .en(1'b1), .Q(test_num), .clk(clock_1_out));  // open: clr
  Adder adder_1 (.a(8'h1), .b(test_num), .out(adder_1_out));  // open: cin, cout
  ROM #(.dataWidth(32)) rom_1 (.addr(test_num), .data(WriteData), .sel(1'b1));
  ROM #(.dataWidth(16)) rom_2 (.addr(test_num), .data(rom_2_data), .sel(1'b1));
  Clock clock_1 (.out(clock_1_out));
  regfile_main main_1 (
    .Read_Register_1__rs1(rom_2_data[4:0]), .Read_Register_2__rs2(rom_2_data[9:5]),
    .Write_Register__rd(rom_2_data[14:10]), .Write_Data(WriteData), .Write_Enable(rom_2_data[15]),
    .Clock(clock_1_out), .Read_Data_1(Read_Data_1), .Read_Data_2(Read_Data_2), .ra_Value(ra_Value),
    .sp_Value(sp_Value), .t0_Value(t0_Value), .t1_Value(t1_Value), .t2_Value(t2_Value), .s0_Value(s0_Value),
    .s1_Value(s1_Value), .a0_Value(a0_Value));

  // Notes on the sheet:
  //   YOUR REGFILE SHOULD FIT IN HERE!
  //   There should be no blue/red wires here, and the result shouldn't be x's.
endmodule
