// Logisim project regfile.circ as structural Verilog: 1 circuit, main circuit main
module main (
  input  [4:0] Read_Register_1__rs1,
  input  [4:0] Read_Register_2__rs2,
  input  [4:0] Write_Register__rd,
  input  [31:0] Write_Data,
  input  Write_Enable,
  input  Clock,
  output [31:0] ra_Value,
  output [31:0] sp_Value,
  output [31:0] t0_Value,
  output [31:0] t1_Value,
  output [31:0] t2_Value,
  output [31:0] s0_Value,
  output [31:0] s1_Value,
  output [31:0] a0_Value,
  output [31:0] Read_Data_1,
  output [31:0] Read_Data_2
);

  wire a0, a1, ra, s0, s1, sp, t0, t1, t2;
  wire [31:0] a1_Value, x1, x2, x5, x6, x7, x8, x9, x10, x11;

  Demultiplexer #(.select(5), .enable("false")) demultiplexer_1 (
    .out1(ra), .out2(sp), .out5(t0), .out6(t1), .out7(t2), .out8(s0), .out9(s1), .out10(a0), .out11(a1),
    .in(Write_Enable), .sel(Write_Register__rd));  // open: out0, out3, out4, out12, out13, out14, out15, out16, out17, out18, out19, out20, out21, out22, out23, out24, out25, out26, out27, out28, out29, out30, out31
  Register #(.width(32)) register_1 (.D(x5), .en(t0), .Q(t0_Value), .clk(Clock));  // open: clr
  Register #(.width(32)) register_2 (.D(x6), .en(t1), .Q(t1_Value), .clk(Clock));  // open: clr
  Register #(.width(32)) register_3 (.D(x1), .en(ra), .Q(ra_Value), .clk(Clock));  // open: clr
  Register #(.width(32)) register_4 (.D(x2), .en(sp), .Q(sp_Value), .clk(Clock));  // open: clr
  Register #(.width(32)) register_5 (.D(x7), .en(t2), .Q(t2_Value), .clk(Clock));  // open: clr
  Register #(.width(32)) register_6 (.D(x8), .en(s0), .Q(s0_Value), .clk(Clock));  // open: clr
  Register #(.width(32)) register_7 (.D(x9), .en(s1), .Q(s1_Value), .clk(Clock));  // open: clr
  Multiplexer #(.select(5), .width(32)) multiplexer_1 (
    .in0({32{1'b0}}), .in1(ra_Value), .in2(sp_Value), .in5(t0_Value), .in6(t1_Value), .in7(t2_Value),
    .in8(s0_Value), .in9(s1_Value), .in10(a0_Value), .in11(a1_Value), .out(Read_Data_2),
    .sel(Read_Register_2__rs2));  // open: in3, in4, in12, in13, in14, in15, in16, in17, in18, in19, in20, in21, in22, in23, in24, in25, in26, in27, in28, in29, in30, in31, en
  Register #(.width(32)) register_8 (.D(x11), .en(a1), .Q(a1_Value), .clk(Clock));  // open: clr
  Demultiplexer #(.select(5), .width(32)) demultiplexer_2 (
    .out1(x1), .out2(x2), .out5(x5), .out6(x6), .out7(x7), .out8(x8), .out9(x9), .out10(x10), .out11(x11),
    .in(Write_Data), .sel(Write_Register__rd), .en(Write_Enable));  // open: out0, out3, out4, out12, out13, out14, out15, out16, out17, out18, out19, out20, out21, out22, out23, out24, out25, out26, out27, out28, out29, out30, out31
  Register #(.width(32)) register_9 (.D(x10), .en(a0), .Q(a0_Value), .clk(Clock));  // open: clr
  Multiplexer #(.select(5), .width(32)) multiplexer_2 (
    .in0({32{1'b0}}), .in1(ra_Value), .in2(sp_Value), .in5(t0_Value), .in6(t1_Value), .in7(t2_Value),
    .in8(s0_Value), .in9(s1_Value), .in10(a0_Value), .in11(a1_Value), .out(Read_Data_1),
    .sel(Read_Register_1__rs1));  // open: in3, in4, in12, in13, in14, in15, in16, in17, in18, in19, in20, in21, in22, in23, in24, in25, in26, in27, in28, in29, in30, in31, en

  // Other names for the same wires on the sheet: clk = Clock; read_data1[31:0] = Read_Data_1;
  //   read_data2[31:0] = Read_Data_2; read_reg1[4:0] = Read_Register_1__rs1; read_reg2[4:0] = Read_Register_2__rs2;
  //   write_en = Write_Enable; write_reg[4:0] = Write_Register__rd

  // Notes on the sheet:
  //   INPUTS to your circuit
  //   These are DEBUG/TEST outputs from your circuit.
  //   OUTPUTS from your circuit
endmodule
