// Logisim project regfile.circ as structural Verilog: 1 circuit, main circuit main
module main (
  input  [4:0] Read_Register_1__rs1,
  input  [4:0] Read_Register_2__rs2,
  input  [4:0] Write_Register__rd,
  input  [31:0] Write_Data,
  input  Write_Enable,
  input  Clock,
  output [31:0] ra_Value,
  output [31:0] sp_Value,
  output [31:0] t0_Value,
  output [31:0] t1_Value,
  output [31:0] t2_Value,
  output [31:0] s0_Value,
  output [31:0] s1_Value,
  output [31:0] a0_Value,
  output [31:0] Read_Data_1,
  output [31:0] Read_Data_2
);

  wire en_a0, en_ra, en_s0, en_s1, en_sp, en_t0, en_t1, en_t2, en_zero;
  wire [31:0] data_a0, data_ra, data_s0, data_s1, data_sp, data_t0, data_t1, data_t2, data_zero, zero;

  Demultiplexer #(.select(5)) demultiplexer_1 (
    .out0(en_zero), .out1(en_ra), .out2(en_sp), .out3(en_t0), .out4(en_t1), .out5(en_t2), .out6(en_s0),
    .out7(en_s1), .out8(en_a0), .in(Write_Enable), .sel(Write_Register__rd));  // open: out9, out10, out11, out12, out13, out14, out15, out16, out17, out18, out19, out20, out21, out22, out23, out24, out25, out26, out27, out28, out29, out30, out31, en
  Register #(.width(32)) register_1 (.Q(zero), .clk(Clock));  // open: D, en, clr
  Demultiplexer #(.select(5), .width(32)) demultiplexer_2 (
    .out0(data_zero), .out1(data_ra), .out2(data_sp), .out3(data_t0), .out4(data_t1), .out5(data_t2),
    .out6(data_s0), .out7(data_s1), .out8(data_a0), .in(Write_Data), .sel(Write_Register__rd),
    .en(Write_Enable));  // open: out9, out10, out11, out12, out13, out14, out15, out16, out17, out18, out19, out20, out21, out22, out23, out24, out25, out26, out27, out28, out29, out30, out31
  Register #(.width(32)) register_2 (.D(data_t0), .en(en_t0), .Q(t0_Value), .clk(Clock));  // open: clr
  Register #(.width(32)) register_3 (.D(data_s0), .en(en_s0), .Q(s0_Value), .clk(Clock));  // open: clr
  Register #(.width(32)) register_4 (.D(data_ra), .en(en_ra), .Q(ra_Value), .clk(Clock));  // open: clr
  Register #(.width(32)) register_5 (.D(data_t1), .en(en_t1), .Q(t1_Value), .clk(Clock));  // open: clr
  Register #(.width(32)) register_6 (.D(data_s1), .en(en_s1), .Q(s1_Value), .clk(Clock));  // open: clr
  Register #(.width(32)) register_7 (.D(data_sp), .en(en_sp), .Q(sp_Value), .clk(Clock));  // open: clr
  Register #(.width(32)) register_8 (.D(data_t2), .en(en_t2), .Q(t2_Value), .clk(Clock));  // open: clr
  Register #(.width(32)) register_9 (.D(data_a0), .en(en_a0), .Q(a0_Value), .clk(Clock));  // open: clr
  Multiplexer #(.select(5), .width(32)) multiplexer_1 (
    .in0(zero), .in1(ra_Value), .in2(sp_Value), .in3(t0_Value), .in4(data_t1), .in5(data_t2), .in6(data_s0),
    .in7(data_s1), .in8(data_a0), .out(Read_Data_1), .sel(Read_Register_1__rs1));  // open: in9, in10, in11, in12, in13, in14, in15, in16, in17, in18, in19, in20, in21, in22, in23, in24, in25, in26, in27, in28, in29, in30, in31, en
  Multiplexer #(.select(5), .width(32)) multiplexer_2 (
    .in0(zero), .in1(ra_Value), .in2(sp_Value), .in3(t0_Value), .in4(data_t1), .in5(data_t2), .in6(data_s0),
    .in7(data_s1), .in8(data_a0), .out(Read_Data_2), .sel(Read_Register_2__rs2));  // open: in9, in10, in11, in12, in13, in14, in15, in16, in17, in18, in19, in20, in21, in22, in23, in24, in25, in26, in27, in28, in29, in30, in31, en

  // Other names for the same wires on the sheet: a0[31:0] = a0_Value; clk = Clock; ra[31:0] = ra_Value;
  //   read_data1[31:0] = Read_Data_1; read_data2[31:0] = Read_Data_2; read_reg1[4:0] = Read_Register_1__rs1;
  //   read_reg2[4:0] = Read_Register_2__rs2; s0[31:0] = s0_Value; s1[31:0] = s1_Value; sp[31:0] = sp_Value;
  //   t0[31:0] = t0_Value; t1[31:0] = t1_Value; t2[31:0] = t2_Value; write_en = Write_Enable;
  //   write_reg[4:0] = Write_Register__rd

  // Notes on the sheet:
  //   INPUTS to your circuit
  //   These are DEBUG/TEST outputs from your circuit.
  //   DON'T CHANGE THE LOCATIONS OF THE INPUTS AND OUTPUTS!
  //   OUTPUTS from your circuit
endmodule
